// Logisim project final-computer.circ as structural Verilog: 22 circuits, main circuit proj1_Register_8Bit
module proj1_Register_8Bit (
  input  [7:0] I,
  input  [1:0] FunSel,
  input  E,
  output [7:0] Q
);

  wire and_2_out, and_3_out, and_4_out, and_5_out, and_6_out, and_7_out, and_8_out, and_9_out, and_10_out,
       and_11_out, and_12_out, and_13_out, and_14_out, and_15_out, and_16_out, and_17_out, and_18_out,
       and_19_out, clock_1_out, decoder_1_out0, decoder_1_out1, decoder_1_out2, decoder_1_out3, not_1_out,
       not_2_out, not_3_out, not_4_out, not_5_out, not_6_out, not_7_out, not_8_out, not_9_out, not_10_out,
       not_11_out, or_1_out, or_2_out, or_3_out, or_4_out, or_5_out, or_6_out, or_7_out, or_8_out, or_9_out,
       or_10_out;
  wire [7:0] adder_1_out, multiplexer_1_out;
  wire [7:7] and_1_out;

  Decoder #(.enable("false"), .select(2)) decoder_1 (
    .out0(decoder_1_out0), .out1(decoder_1_out1), .out2(decoder_1_out2), .out3(decoder_1_out3), .sel(FunSel));
  Hex_Digit_Display hex_digit_display_1 (.value(I[7:4]));  // open: dp
  Hex_Digit_Display hex_digit_display_2 (.value(I[3:0]));  // open: dp
  not not_1 (not_1_out, decoder_1_out2);
  and and_1 (and_1_out[7], not_1_out, decoder_1_out3);
  or or_1 (or_1_out, decoder_1_out2, decoder_1_out3);
  Adder adder_1 (.a(Q), .b({{7{and_1_out[7]}}, 1'b1}), .out(adder_1_out));  // open: cin, cout
  not not_2 (not_2_out, decoder_1_out0);
  or or_2 (or_2_out, or_1_out, decoder_1_out0, decoder_1_out1);
  and and_2 (and_2_out, decoder_1_out1, not_3_out);
  not not_3 (not_3_out, or_1_out);
  and and_3 (and_3_out, E, or_2_out);
  Multiplexer #(.width(8)) multiplexer_1 (
    .in0(adder_1_out), .in1(I), .out(multiplexer_1_out), .sel(and_2_out), .en(not_2_out));
  not not_4 (not_4_out, and_3_out);
  not not_5 (not_5_out, and_3_out);
  not not_6 (not_6_out, and_3_out);
  not not_7 (not_7_out, and_3_out);
  not not_8 (not_8_out, and_3_out);
  not not_9 (not_9_out, and_3_out);
  not not_10 (not_10_out, and_3_out);
  not not_11 (not_11_out, and_3_out);
  and and_4 (and_4_out, Q[0], not_4_out);
  and and_5 (and_5_out, and_3_out, multiplexer_1_out[0]);
  and and_6 (and_6_out, Q[1], not_5_out);
  and and_7 (and_7_out, and_3_out, multiplexer_1_out[1]);
  and and_8 (and_8_out, Q[2], not_6_out);
  and and_9 (and_9_out, and_3_out, multiplexer_1_out[2]);
  and and_10 (and_10_out, Q[3], not_7_out);
  and and_11 (and_11_out, and_3_out, multiplexer_1_out[3]);
  and and_12 (and_12_out, Q[4], not_8_out);
  and and_13 (and_13_out, and_3_out, multiplexer_1_out[4]);
  and and_14 (and_14_out, Q[5], not_9_out);
  and and_15 (and_15_out, and_3_out, multiplexer_1_out[5]);
  and and_16 (and_16_out, Q[6], not_10_out);
  and and_17 (and_17_out, and_3_out, multiplexer_1_out[6]);
  and and_18 (and_18_out, Q[7], not_11_out);
  and and_19 (and_19_out, and_3_out, multiplexer_1_out[7]);
  or or_3 (or_3_out, and_4_out, and_5_out);
  or or_4 (or_4_out, and_6_out, and_7_out);
  or or_5 (or_5_out, and_8_out, and_9_out);
  or or_6 (or_6_out, and_10_out, and_11_out);
  or or_7 (or_7_out, and_12_out, and_13_out);
  or or_8 (or_8_out, and_14_out, and_15_out);
  or or_9 (or_9_out, and_16_out, and_17_out);
  or or_10 (or_10_out, and_18_out, and_19_out);
  D_Flip_Flop d_ff_1 (.D(or_3_out), .clk(clock_1_out), .Q(Q[0]));  // open: Qn, preset, reset
  D_Flip_Flop d_ff_2 (.D(or_4_out), .clk(clock_1_out), .Q(Q[1]));  // open: Qn, preset, reset
  D_Flip_Flop d_ff_3 (.D(or_5_out), .clk(clock_1_out), .Q(Q[2]));  // open: Qn, preset, reset
  D_Flip_Flop d_ff_4 (.D(or_6_out), .clk(clock_1_out), .Q(Q[3]));  // open: Qn, preset, reset
  D_Flip_Flop d_ff_5 (.D(or_7_out), .clk(clock_1_out), .Q(Q[4]));  // open: Qn, preset, reset
  D_Flip_Flop d_ff_6 (.D(or_8_out), .clk(clock_1_out), .Q(Q[5]));  // open: Qn, preset, reset
  D_Flip_Flop d_ff_7 (.D(or_9_out), .clk(clock_1_out), .Q(Q[6]));  // open: Qn, preset, reset
  D_Flip_Flop d_ff_8 (.D(or_10_out), .clk(clock_1_out), .Q(Q[7]));  // open: Qn, preset, reset
  Clock clock_1 (.out(clock_1_out));
  Hex_Digit_Display hex_digit_display_3 (.value(Q[7:4]));  // open: dp
  Hex_Digit_Display hex_digit_display_4 (.value(Q[3:0]));  // open: dp
endmodule

module proj1_Register_16Bit (
  input  [15:0] I,
  input  [1:0] FunSel,
  input  E,
  output [15:0] Q
);

  wire and_2_out, and_3_out, and_4_out, and_5_out, and_6_out, and_7_out, and_8_out, and_9_out, and_10_out,
       and_11_out, and_12_out, and_13_out, and_14_out, and_15_out, and_16_out, and_17_out, and_18_out,
       and_19_out, and_20_out, and_21_out, and_22_out, and_23_out, and_24_out, and_25_out, and_26_out,
       and_27_out, and_28_out, and_29_out, and_30_out, and_31_out, and_32_out, and_33_out, and_34_out,
       and_35_out, clock_1_out, decoder_1_out0, decoder_1_out1, decoder_1_out2, decoder_1_out3, not_1_out,
       not_2_out, not_3_out, not_4_out, not_5_out, not_6_out, not_7_out, not_8_out, not_9_out, not_10_out,
       not_11_out, not_12_out, not_13_out, not_14_out, not_15_out, not_16_out, not_17_out, not_18_out,
       not_19_out, or_1_out, or_2_out, or_3_out, or_4_out, or_5_out, or_6_out, or_7_out, or_8_out, or_9_out,
       or_10_out, or_11_out, or_12_out, or_13_out, or_14_out, or_15_out, or_16_out, or_17_out, or_18_out;
  wire [15:0] adder_1_out, multiplexer_1_out;
  wire [15:15] and_1_out;

  Hex_Digit_Display hex_digit_display_1 (.value(I[15:12]));  // open: dp
  Hex_Digit_Display hex_digit_display_2 (.value(I[11:8]));  // open: dp
  Decoder #(.enable("false"), .select(2)) decoder_1 (
    .out0(decoder_1_out0), .out1(decoder_1_out1), .out2(decoder_1_out2), .out3(decoder_1_out3), .sel(FunSel));
  Hex_Digit_Display hex_digit_display_3 (.value(I[7:4]));  // open: dp
  Hex_Digit_Display hex_digit_display_4 (.value(I[3:0]));  // open: dp
  not not_1 (not_1_out, decoder_1_out2);
  and and_1 (and_1_out[15], not_1_out, decoder_1_out3);
  or or_1 (or_1_out, decoder_1_out2, decoder_1_out3);
  Adder #(.width(16)) adder_1 (.a(Q), .b({{15{and_1_out[15]}}, 1'b1}), .out(adder_1_out));  // open: cin, cout
  not not_2 (not_2_out, decoder_1_out0);
  or or_2 (or_2_out, or_1_out, decoder_1_out0, decoder_1_out1);
  Multiplexer #(.width(16)) multiplexer_1 (
    .in0(adder_1_out), .in1(I), .out(multiplexer_1_out), .sel(and_2_out), .en(not_2_out));
  and and_2 (and_2_out, decoder_1_out1, not_3_out);
  not not_3 (not_3_out, or_1_out);
  and and_3 (and_3_out, E, or_2_out);
  not not_4 (not_4_out, and_3_out);
  not not_5 (not_5_out, and_3_out);
  not not_6 (not_6_out, and_3_out);
  not not_7 (not_7_out, and_3_out);
  not not_8 (not_8_out, and_3_out);
  not not_9 (not_9_out, and_3_out);
  not not_10 (not_10_out, and_3_out);
  not not_11 (not_11_out, and_3_out);
  not not_12 (not_12_out, and_3_out);
  not not_13 (not_13_out, and_3_out);
  not not_14 (not_14_out, and_3_out);
  not not_15 (not_15_out, and_3_out);
  not not_16 (not_16_out, and_3_out);
  not not_17 (not_17_out, and_3_out);
  not not_18 (not_18_out, and_3_out);
  not not_19 (not_19_out, and_3_out);
  and and_4 (and_4_out, Q[0], not_4_out);
  and and_5 (and_5_out, and_3_out, multiplexer_1_out[0]);
  and and_6 (and_6_out, Q[1], not_5_out);
  and and_7 (and_7_out, and_3_out, multiplexer_1_out[1]);
  and and_8 (and_8_out, Q[2], not_6_out);
  and and_9 (and_9_out, and_3_out, multiplexer_1_out[2]);
  and and_10 (and_10_out, Q[3], not_7_out);
  and and_11 (and_11_out, and_3_out, multiplexer_1_out[3]);
  and and_12 (and_12_out, Q[4], not_8_out);
  and and_13 (and_13_out, and_3_out, multiplexer_1_out[4]);
  and and_14 (and_14_out, Q[5], not_9_out);
  and and_15 (and_15_out, and_3_out, multiplexer_1_out[5]);
  and and_16 (and_16_out, Q[6], not_10_out);
  and and_17 (and_17_out, and_3_out, multiplexer_1_out[6]);
  and and_18 (and_18_out, Q[7], not_11_out);
  and and_19 (and_19_out, and_3_out, multiplexer_1_out[7]);
  and and_20 (and_20_out, Q[8], not_12_out);
  and and_21 (and_21_out, and_3_out, multiplexer_1_out[8]);
  and and_22 (and_22_out, Q[9], not_13_out);
  and and_23 (and_23_out, and_3_out, multiplexer_1_out[9]);
  and and_24 (and_24_out, Q[10], not_14_out);
  and and_25 (and_25_out, and_3_out, multiplexer_1_out[10]);
  and and_26 (and_26_out, Q[11], not_15_out);
  and and_27 (and_27_out, and_3_out, multiplexer_1_out[11]);
  and and_28 (and_28_out, Q[12], not_16_out);
  and and_29 (and_29_out, and_3_out, multiplexer_1_out[12]);
  and and_30 (and_30_out, Q[13], not_17_out);
  and and_31 (and_31_out, and_3_out, multiplexer_1_out[13]);
  and and_32 (and_32_out, Q[14], not_18_out);
  and and_33 (and_33_out, and_3_out, multiplexer_1_out[14]);
  and and_34 (and_34_out, Q[15], not_19_out);
  and and_35 (and_35_out, and_3_out, multiplexer_1_out[15]);
  or or_3 (or_3_out, and_4_out, and_5_out);
  or or_4 (or_4_out, and_6_out, and_7_out);
  or or_5 (or_5_out, and_8_out, and_9_out);
  or or_6 (or_6_out, and_10_out, and_11_out);
  or or_7 (or_7_out, and_12_out, and_13_out);
  or or_8 (or_8_out, and_14_out, and_15_out);
  or or_9 (or_9_out, and_16_out, and_17_out);
  or or_10 (or_10_out, and_18_out, and_19_out);
  or or_11 (or_11_out, and_20_out, and_21_out);
  or or_12 (or_12_out, and_22_out, and_23_out);
  or or_13 (or_13_out, and_24_out, and_25_out);
  or or_14 (or_14_out, and_26_out, and_27_out);
  or or_15 (or_15_out, and_28_out, and_29_out);
  or or_16 (or_16_out, and_30_out, and_31_out);
  or or_17 (or_17_out, and_32_out, and_33_out);
  or or_18 (or_18_out, and_34_out, and_35_out);
  D_Flip_Flop d_ff_1 (.D(or_3_out), .clk(clock_1_out), .Q(Q[0]));  // open: Qn, preset, reset
  D_Flip_Flop d_ff_2 (.D(or_4_out), .clk(clock_1_out), .Q(Q[1]));  // open: Qn, preset, reset
  D_Flip_Flop d_ff_3 (.D(or_5_out), .clk(clock_1_out), .Q(Q[2]));  // open: Qn, preset, reset
  D_Flip_Flop d_ff_4 (.D(or_6_out), .clk(clock_1_out), .Q(Q[3]));  // open: Qn, preset, reset
  D_Flip_Flop d_ff_5 (.D(or_7_out), .clk(clock_1_out), .Q(Q[4]));  // open: Qn, preset, reset
  D_Flip_Flop d_ff_6 (.D(or_8_out), .clk(clock_1_out), .Q(Q[5]));  // open: Qn, preset, reset
  D_Flip_Flop d_ff_7 (.D(or_9_out), .clk(clock_1_out), .Q(Q[6]));  // open: Qn, preset, reset
  D_Flip_Flop d_ff_8 (.D(or_10_out), .clk(clock_1_out), .Q(Q[7]));  // open: Qn, preset, reset
  D_Flip_Flop d_ff_9 (.D(or_11_out), .clk(clock_1_out), .Q(Q[8]));  // open: Qn, preset, reset
  D_Flip_Flop d_ff_10 (.D(or_12_out), .clk(clock_1_out), .Q(Q[9]));  // open: Qn, preset, reset
  D_Flip_Flop d_ff_11 (.D(or_13_out), .clk(clock_1_out), .Q(Q[10]));  // open: Qn, preset, reset
  D_Flip_Flop d_ff_12 (.D(or_14_out), .clk(clock_1_out), .Q(Q[11]));  // open: Qn, preset, reset
  D_Flip_Flop d_ff_13 (.D(or_15_out), .clk(clock_1_out), .Q(Q[12]));  // open: Qn, preset, reset
  D_Flip_Flop d_ff_14 (.D(or_16_out), .clk(clock_1_out), .Q(Q[13]));  // open: Qn, preset, reset
  D_Flip_Flop d_ff_15 (.D(or_17_out), .clk(clock_1_out), .Q(Q[14]));  // open: Qn, preset, reset
  D_Flip_Flop d_ff_16 (.D(or_18_out), .clk(clock_1_out), .Q(Q[15]));  // open: Qn, preset, reset
  Clock clock_1 (.out(clock_1_out));
  Hex_Digit_Display hex_digit_display_5 (.value(Q[15:12]));  // open: dp
  Hex_Digit_Display hex_digit_display_6 (.value(Q[11:8]));  // open: dp
  Hex_Digit_Display hex_digit_display_7 (.value(Q[7:4]));  // open: dp
  Hex_Digit_Display hex_digit_display_8 (.value(Q[3:0]));  // open: dp
endmodule

module proj1_RegFile_2a (
  input  [7:0] I,
  input  [3:0] RegSel,
  input  [1:0] FunSel,
  input  [1:0] OutASel,
  input  [1:0] OutBSel,
  output [7:0] OutA,
  output [7:0] OutB
);

  wire [7:0] R0_q, R1_q, R2_q, R3_q;

  Hex_Digit_Display hex_digit_display_1 (.value(I[7:4]));  // open: dp
  Hex_Digit_Display hex_digit_display_2 (.value(I[3:0]));  // open: dp
  proj1_Register_8Bit R3 (.Q(R3_q), .FunSel(FunSel), .I(I), .E(RegSel[3]));
  proj1_Register_8Bit R2 (.Q(R2_q), .FunSel(FunSel), .I(I), .E(RegSel[2]));
  proj1_Register_8Bit R1 (.Q(R1_q), .FunSel(FunSel), .I(I), .E(RegSel[1]));
  proj1_Register_8Bit R0 (.Q(R0_q), .FunSel(FunSel), .I(I), .E(RegSel[0]));
  Multiplexer #(.enable("false"), .select(2), .width(8)) multiplexer_1 (
    .in0(R0_q), .in1(R1_q), .in2(R2_q), .in3(R3_q), .out(OutA), .sel(OutASel));
  Multiplexer #(.enable("false"), .select(2), .width(8)) multiplexer_2 (
    .in0(R0_q), .in1(R1_q), .in2(R2_q), .in3(R3_q), .out(OutB), .sel(OutBSel));
  Hex_Digit_Display hex_digit_display_3 (.value(OutA[7:4]));  // open: dp
  Hex_Digit_Display hex_digit_display_4 (.value(OutB[7:4]));  // open: dp
  Hex_Digit_Display hex_digit_display_5 (.value(OutA[3:0]));  // open: dp
  Hex_Digit_Display hex_digit_display_6 (.value(OutB[3:0]));  // open: dp
endmodule

module proj1_RegFile_2b (
  input  [7:0] I,
  input  [2:0] RegSel,
  input  [1:0] FunSel,
  input  [1:0] OutCSel,
  input  [1:0] OutDSel,
  output [7:0] OutC,
  output [7:0] OutD
);

  wire [7:0] AR_q, PC_q, SP_q;

  Hex_Digit_Display hex_digit_display_1 (.value(I[7:4]));  // open: dp
  Hex_Digit_Display hex_digit_display_2 (.value(I[3:0]));  // open: dp
  proj1_Register_8Bit SP (.Q(SP_q), .FunSel(FunSel), .I(I), .E(RegSel[2]));
  proj1_Register_8Bit AR (.Q(AR_q), .FunSel(FunSel), .I(I), .E(RegSel[1]));
  proj1_Register_8Bit PC (.Q(PC_q), .FunSel(FunSel), .I(I), .E(RegSel[0]));
  Multiplexer #(.enable("false"), .select(2), .width(8)) multiplexer_1 (
    .in0(PC_q), .in1(AR_q), .in2(SP_q), .in3(PC_q), .out(OutC), .sel(OutCSel));
  Multiplexer #(.enable("false"), .select(2), .width(8)) multiplexer_2 (
    .in0(PC_q), .in1(AR_q), .in2(SP_q), .in3(PC_q), .out(OutD), .sel(OutDSel));
  Hex_Digit_Display hex_digit_display_3 (.value(OutC[7:4]));  // open: dp
  Hex_Digit_Display hex_digit_display_4 (.value(OutD[7:4]));  // open: dp
  Hex_Digit_Display hex_digit_display_5 (.value(OutC[3:0]));  // open: dp
  Hex_Digit_Display hex_digit_display_6 (.value(OutD[3:0]));  // open: dp
endmodule

module proj1_IR (
  input  [7:0] I,
  input  H,
  input  Enable,
  input  [1:0] FunSel,
  output [15:0] IRout
);

  wire and_1_out, and_2_out, and_3_out, isDec_out, isEmpty_out, isFull_out, isInc_out, nor_1_out, not_1_out,
       not_2_out, not_3_out, not_4_out;
  wire [1:0] multiplexer_3_out, multiplexer_4_out, multiplexer_5_out, multiplexer_6_out;
  wire [1:1] or_1_out;
  wire [7:0] multiplexer_1_out, multiplexer_2_out;

  Hex_Digit_Display hex_digit_display_1 (.value(I[7:4]));  // open: dp
  Hex_Digit_Display hex_digit_display_2 (.value(I[3:0]));  // open: dp
  not not_1 (not_1_out, FunSel[1]);
  not not_2 (not_2_out, FunSel[0]);
  and and_1 (and_1_out, H, nor_1_out);
  and and_2 (and_2_out, not_1_out, FunSel[0]);
  and and_3 (and_3_out, FunSel[1], not_2_out);
  or or_1 (or_1_out[1], and_2_out, and_3_out);
  Multiplexer #(.enable("false"), .width(8)) multiplexer_1 (
    .in0(IRout[15:8]), .in1(I), .out(multiplexer_1_out), .sel(and_1_out));
  proj1_Register_8Bit IR_H (.Q(IRout[15:8]), .FunSel(multiplexer_3_out), .I(multiplexer_1_out), .E(Enable));
  not not_3 (not_3_out, FunSel[1]);
  and isInc (isInc_out, not_3_out, or_1_out[1]);
  and isDec (isDec_out, FunSel[1], or_1_out[1]);
  Multiplexer #(.enable("false"), .width(8)) multiplexer_2 (
    .in0(I), .in1(IRout[7:0]), .out(multiplexer_2_out), .sel(and_1_out));
  proj1_Register_8Bit IR_L (.Q(IRout[7:0]), .FunSel({or_1_out[1], FunSel[1]}), .I(multiplexer_2_out), .E(Enable));
  not not_4 (not_4_out, isDec_out);
  Hex_Digit_Display hex_digit_display_3 (.value(IRout[15:12]));  // open: dp
  and isFull (isFull_out, IRout[0], IRout[1], IRout[2], IRout[3], IRout[4], IRout[5], IRout[6], IRout[7], isInc_out);
  nor isEmpty (isEmpty_out, IRout[0], IRout[1], IRout[2], IRout[3], IRout[4], IRout[5], IRout[6], IRout[7], not_4_out);
  nor nor_1 (nor_1_out, isInc_out, isDec_out);
  Hex_Digit_Display hex_digit_display_4 (.value(IRout[11:8]));  // open: dp
  Hex_Digit_Display hex_digit_display_5 (.value(IRout[7:4]));  // open: dp
  Multiplexer #(.enable("false"), .width(2)) multiplexer_3 (
    .in0(multiplexer_6_out), .in1({or_1_out[1], FunSel[1]}), .out(multiplexer_3_out), .sel(nor_1_out));
  Hex_Digit_Display hex_digit_display_6 (.value(IRout[3:0]));  // open: dp
  Multiplexer #(.disabled("Z"), .enable("false"), .width(2)) multiplexer_4 (
    .in0(2'b01), .in1(2'b10), .out(multiplexer_4_out), .sel(isFull_out));
  Multiplexer #(.disabled("Z"), .enable("false"), .width(2)) multiplexer_5 (
    .in0(2'b01), .in1(2'b11), .out(multiplexer_5_out), .sel(isEmpty_out));
  Multiplexer #(.enable("false"), .width(2)) multiplexer_6 (
    .in0(multiplexer_4_out), .in1(multiplexer_5_out), .out(multiplexer_6_out), .sel(isEmpty_out));

  // Notes on the sheet:
  //   Fatih Uzunoğlu. 08/03/2020
endmodule

module proj1_IR2_ver2 (
  input  H,
  input  [7:0] I,
  input  Enable,
  input  [1:0] FunSel,
  output [7:0] IR_L,
  output [7:0] IR_H
);

  wire and_1_out, and_2_out, not_1_out, not_2_out;
  wire [1:1] or_1_out;
  wire [15:0] multiplexer_1_out;

  Hex_Digit_Display hex_digit_display_1 (.value(I[7:4]));  // open: dp
  Hex_Digit_Display hex_digit_display_2 (.value(I[3:0]));  // open: dp
  not not_1 (not_1_out, FunSel[1]);
  not not_2 (not_2_out, FunSel[0]);
  and and_1 (and_1_out, not_1_out, FunSel[0]);
  and and_2 (and_2_out, FunSel[1], not_2_out);
  or or_1 (or_1_out[1], and_1_out, and_2_out);
  Multiplexer #(.enable("false"), .width(16)) multiplexer_1 (
    .in0({IR_H, I}), .in1({I, IR_L}), .out(multiplexer_1_out), .sel(H));
  proj1_Register_16Bit IR (.Q({IR_H, IR_L}), .FunSel({or_1_out[1], FunSel[1]}), .I(multiplexer_1_out), .E(Enable));
  Hex_Digit_Display hex_digit_display_3 (.value(IR_H[7:4]));  // open: dp
  Hex_Digit_Display hex_digit_display_4 (.value(IR_L[7:4]));  // open: dp
  Hex_Digit_Display hex_digit_display_5 (.value(IR_H[3:0]));  // open: dp
  Hex_Digit_Display hex_digit_display_6 (.value(IR_L[3:0]));  // open: dp
endmodule

module proj2_flagRegister (
  input  [3:0] in_1,
  output O,
  output N,
  output C,
  output Z
);

  wire clock_1_out;

  D_Flip_Flop d_ff_1 (.D(in_1[0]), .clk(clock_1_out), .Q(O));  // open: Qn, preset, reset
  D_Flip_Flop d_ff_2 (.D(in_1[1]), .clk(clock_1_out), .Q(N));  // open: Qn, preset, reset
  D_Flip_Flop d_ff_3 (.D(in_1[2]), .clk(clock_1_out), .Q(C));  // open: Qn, preset, reset
  D_Flip_Flop d_ff_4 (.D(in_1[3]), .clk(clock_1_out), .Q(Z));  // open: Qn, preset, reset
  Clock clock_1 (.out(clock_1_out));
  LED OLed (.in(O));
  LED NLed (.in(N));
  LED CLed (.in(C));
  LED ZLed (.in(Z));
endmodule

module proj2_ALU_arithmeticUnit (
  input  Carry,
  input  [1:0] mode,
  input  [7:0] A,
  input  [7:0] B,
  output Z,
  output [7:0] aOut,
  output C,
  output O,
  output N
);

  wire adder_1_cout, and_1_out, and_2_out, and_3_out, and_4_out, and_5_out, borrowToCarry_out,
       decoder_1_out1, decoder_1_out2, not_1_out, not_2_out, not_3_out, not_4_out, not_5_out, not_6_out,
       or_1_out, or_2_out, subtractor_1_bout;
  wire [7:0] adder_1_out, subtractor_1_out;

  Decoder #(.enable("false"), .select(2)) decoder_1 (
    .out1(decoder_1_out1), .out2(decoder_1_out2), .sel(mode));  // open: out0, out3
  and and_1 (and_1_out, Carry, decoder_1_out1);
  Adder adder_1 (.a(A), .b(B), .out(adder_1_out), .cin(and_1_out), .cout(adder_1_cout));
  Subtractor subtractor_1 (.a(A), .b(B), .out(subtractor_1_out), .bout(subtractor_1_bout));  // open: bin
  not not_1 (not_1_out, A[7]);
  not not_2 (not_2_out, B[7]);
  not not_3 (not_3_out, aOut[7]);
  not not_4 (not_4_out, A[7]);
  not not_5 (not_5_out, B[7]);
  not not_6 (not_6_out, aOut[7]);
  and and_2 (and_2_out, not_1_out, not_2_out, aOut[7]);
  and and_3 (and_3_out, A[7], B[7], not_3_out);
  and and_4 (and_4_out, not_4_out, B[7], aOut[7]);
  and and_5 (and_5_out, A[7], not_5_out, not_6_out);
  Multiplexer #(.enable("false"), .width(8)) multiplexer_1 (
    .in0(adder_1_out), .in1(subtractor_1_out), .out(aOut), .sel(decoder_1_out2));
  Multiplexer #(.enable("false")) multiplexer_2 (
    .in0(adder_1_cout), .in1(borrowToCarry_out), .out(C), .sel(decoder_1_out2));
  not borrowToCarry (borrowToCarry_out, subtractor_1_bout);
  or or_1 (or_1_out, and_2_out, and_3_out);
  or or_2 (or_2_out, and_4_out, and_5_out);
  Multiplexer #(.enable("false")) multiplexer_3 (.in0(or_1_out), .in1(or_2_out), .out(O), .sel(decoder_1_out2));
  nor nor_1 (Z, aOut[0], aOut[1], aOut[2], aOut[3], aOut[4], aOut[5], aOut[6], aOut[7]);

  assign N = aOut[7];
endmodule

module proj2_ALU_shiftUnit (
  input  [7:0] inputVar,
  input  [2:0] mode,
  input  Carry,
  output C,
  output [7:0] sOut,
  output Z,
  output N,
  output O
);

  wire xor_1_out, xor_2_out, xor_3_out;

  Multiplexer #(.enable("false"), .select(3)) multiplexer_1 (
    .in0(inputVar[7]), .in1(inputVar[0]), .in4(inputVar[7]), .in5(inputVar[0]), .out(C), .sel(mode));  // open: in2, in3, in6, in7
  xor xor_1 (xor_1_out, inputVar[7], inputVar[6]);
  xor xor_2 (xor_2_out, inputVar[6], inputVar[7]);
  xor xor_3 (xor_3_out, inputVar[7], Carry);
  Multiplexer #(.enable("false"), .select(3), .width(8)) multiplexer_2 (
    .in0({inputVar[6:0], 1'b0}), .in1({1'b0, inputVar[7:1]}), .in2({inputVar[6:0], 1'b0}),
    .in3({{2{inputVar[7]}}, inputVar[6:1]}), .in4({inputVar[6:0], Carry}), .in5({Carry, inputVar[7:1]}),
    .out({N, sOut[6:0]}), .sel(mode));  // open: in6, in7
  Multiplexer #(.enable("false"), .select(3)) multiplexer_3 (
    .in2(xor_1_out), .in4(xor_2_out), .in5(xor_3_out), .out(O), .sel(mode));  // open: in0, in1, in3, in6, in7
  nor nor_1 (Z, sOut[0], sOut[1], sOut[2], sOut[3], sOut[4], sOut[5], sOut[6], N);

  assign sOut[7] = N;
endmodule

module proj2_ALU_logicUnit (
  input  [7:0] A,
  input  [7:0] B,
  input  [2:0] mode,
  output Z,
  output N,
  output [7:0] lOut
);

  wire [7:0] and_1_out, not_1_out, not_2_out, or_1_out, xor_1_out;

  assign not_1_out = ~A;  // NOT_Gate not_1, 8 bits wide
  assign not_2_out = ~B;  // NOT_Gate not_2, 8 bits wide
  Multiplexer #(.enable("false"), .select(3), .width(8)) multiplexer_1 (
    .in0(A), .in1(B), .in2(not_1_out), .in3(not_2_out), .in4(and_1_out), .in5(or_1_out), .in6(xor_1_out),
    .out(lOut), .sel(mode));  // open: in7
  assign and_1_out = A & B;  // AND_Gate and_1, 8 bits wide
  assign or_1_out = A | B;  // OR_Gate or_1, 8 bits wide
  nor nor_1 (Z, lOut[0], lOut[1], lOut[2], lOut[3], lOut[4], lOut[5], lOut[6], lOut[7]);
  assign xor_1_out = A ^ B;  // XOR_Gate xor_1, 8 bits wide

  assign N = lOut[7];
endmodule

module proj2_ALU_implementation (
  input  [7:0] A,
  input  Cin,
  input  [7:0] B,
  input  [3:0] FunSel,
  output [3:0] Flags_ZCNO,
  output [7:0] OutAlu
);

  wire and_1_out, and_2_out, and_3_out, and_4_out, and_6_out, and_7_out, and_8_out, and_9_out, not_1_out,
       not_2_out, not_3_out, proj2_alu_arithmeticunit_1_c, proj2_alu_arithmeticunit_1_n,
       proj2_alu_arithmeticunit_1_o, proj2_alu_arithmeticunit_1_z, proj2_alu_logicunit_1_n,
       proj2_alu_logicunit_1_z, proj2_alu_shiftunit_1_c, proj2_alu_shiftunit_1_n, proj2_alu_shiftunit_1_o,
       proj2_alu_shiftunit_1_z;
  wire [1:0] or_5_out;
  wire [2:0] or_3_out;
  wire [2:1] not_4_out;
  wire [7:0] proj2_alu_arithmeticunit_1_aout, proj2_alu_logicunit_1_lout, proj2_alu_shiftunit_1_sout;

  or or_1 (or_3_out[2], FunSel[3], FunSel[2]);
  and and_1 (and_1_out, FunSel[0], FunSel[3]);
  or or_2 (or_3_out[1], and_1_out, and_2_out);
  not not_1 (not_1_out, FunSel[3]);
  and and_2 (and_2_out, FunSel[1], not_2_out);
  and and_3 (and_3_out, not_1_out, not_2_out, FunSel[0]);
  not not_2 (not_2_out, FunSel[2]);
  not not_3 (not_3_out, FunSel[0]);
  and and_4 (and_4_out, FunSel[3], not_3_out);
  or or_3 (or_3_out[0], and_3_out, and_4_out);
  and and_5 (not_4_out[2], FunSel[2], FunSel[1]);
  not not_4 (not_4_out[1], FunSel[1]);
  proj2_ALU_logicUnit proj2_alu_logicunit_1 (
    .lOut(proj2_alu_logicunit_1_lout), .Z(proj2_alu_logicunit_1_z), .N(proj2_alu_logicunit_1_n),
    .mode(or_3_out), .A(A), .B(B));
  and and_6 (and_6_out, FunSel[2], FunSel[3]);
  and and_7 (and_7_out, FunSel[1], FunSel[3]);
  and and_8 (and_8_out, ~FunSel[3], FunSel[2], ~FunSel[1]);  // AND_Gate
  and and_9 (and_9_out, ~FunSel[3], FunSel[2], ~FunSel[0]);  // AND_Gate
  proj2_ALU_shiftUnit proj2_alu_shiftunit_1 (
    .C(proj2_alu_shiftunit_1_c), .O(proj2_alu_shiftunit_1_o), .sOut(proj2_alu_shiftunit_1_sout),
    .N(proj2_alu_shiftunit_1_n), .Z(proj2_alu_shiftunit_1_z), .inputVar(A), .Carry(Cin),
    .mode({not_4_out, FunSel[0]}));
  or or_4 (or_5_out[1], and_6_out, and_7_out);
  or or_5 (or_5_out[0], and_8_out, and_9_out);
  proj2_ALU_arithmeticUnit proj2_alu_arithmeticunit_1 (
    .N(proj2_alu_arithmeticunit_1_n), .aOut(proj2_alu_arithmeticunit_1_aout),
    .C(proj2_alu_arithmeticunit_1_c), .O(proj2_alu_arithmeticunit_1_o), .Z(proj2_alu_arithmeticunit_1_z),
    .A(A), .B(B), .mode(FunSel[1:0]), .Carry(Cin));
  Multiplexer #(.disabled("Z"), .enable("false"), .select(2), .width(8)) multiplexer_1 (
    .in0(proj2_alu_logicunit_1_lout), .in1(proj2_alu_arithmeticunit_1_aout),
    .in2(proj2_alu_shiftunit_1_sout), .out(OutAlu), .sel(or_5_out));  // open: in3
  Multiplexer #(.disabled("Z"), .enable("false"), .select(2)) multiplexer_2 (
    .in0(proj2_alu_logicunit_1_z), .in1(proj2_alu_arithmeticunit_1_z), .in2(proj2_alu_shiftunit_1_z),
    .out(Flags_ZCNO[3]), .sel(or_5_out));  // open: in3
  Multiplexer #(.disabled("Z"), .enable("false"), .select(2)) multiplexer_3 (
    .in1(proj2_alu_arithmeticunit_1_c), .in2(proj2_alu_shiftunit_1_c), .out(Flags_ZCNO[2]), .sel(or_5_out));  // open: in0, in3
  Multiplexer #(.disabled("Z"), .enable("false"), .select(2)) multiplexer_4 (
    .in1(proj2_alu_arithmeticunit_1_o), .in2(proj2_alu_shiftunit_1_o), .out(Flags_ZCNO[0]), .sel(or_5_out));  // open: in0, in3
  Multiplexer #(.disabled("Z"), .enable("false"), .select(2)) multiplexer_5 (
    .in0(proj2_alu_logicunit_1_n), .in1(proj2_alu_arithmeticunit_1_n), .in2(proj2_alu_shiftunit_1_n),
    .out(Flags_ZCNO[1]), .sel(or_5_out));  // open: in3
endmodule

module proj2_ALU_testbed (
  input  [7:0] in_1,
  input  [7:0] in_2,
  input  [3:0] FunSel,
  output [7:0] out_4
);

  wire proj2_flagregister_1_c;
  wire [3:0] proj2_alu_implementation_1_flags_zcno;

  Hex_Digit_Display hex_digit_display_1 (.value(in_1[7:4]));  // open: dp
  Hex_Digit_Display hex_digit_display_2 (.value(in_2[7:4]));  // open: dp
  Hex_Digit_Display hex_digit_display_3 (.value(in_1[3:0]));  // open: dp
  Hex_Digit_Display hex_digit_display_4 (.value(in_2[3:0]));  // open: dp
  proj2_ALU_implementation proj2_alu_implementation_1 (
    .OutAlu(out_4), .Flags_ZCNO(proj2_alu_implementation_1_flags_zcno), .FunSel(FunSel), .A(in_2), .B(in_1),
    .Cin(proj2_flagregister_1_c));
  Hex_Digit_Display hex_digit_display_5 (.value(out_4[7:4]));  // open: dp
  proj2_flagRegister proj2_flagregister_1 (
    .C(proj2_flagregister_1_c), .in_1(proj2_alu_implementation_1_flags_zcno));  // open: O, N, Z
  Hex_Digit_Display hex_digit_display_6 (.value(out_4[3:0]));  // open: dp
endmodule

module proj3_Organization (
);

  wire clock_1_out, final_controlunit_1_ir_enable, final_controlunit_1_ir_selh, final_controlunit_1_muxcsel,
       final_controlunit_1_ram_writeenable, proj2_flagregister_1_c, proj2_flagregister_1_z;
  wire [1:0] final_controlunit_1_ar_funsel, final_controlunit_1_gpr_funsel, final_controlunit_1_ir_funsel,
       final_controlunit_1_muxasel, final_controlunit_1_muxbsel, final_controlunit_1_outasel,
       final_controlunit_1_outbsel, final_controlunit_1_outcsel, final_controlunit_1_outdsel;
  wire [2:0] final_controlunit_1_ar_regsel;
  wire [3:0] final_controlunit_1_alu_funsel, final_controlunit_1_gpr_regsel,
       proj2_alu_implementation_1_flags_zcno;
  wire [7:0] multiplexer_1_out, multiplexer_2_out, multiplexer_3_out, proj1_ir2_ver2_1_ir_h,
       proj1_ir2_ver2_1_ir_l, proj1_regfile_2a_1_outa, proj1_regfile_2a_1_outb, proj1_regfile_2b_1_outc,
       proj1_regfile_2b_1_outd, proj2_alu_implementation_1_outalu, ram_1_dout;

  Multiplexer #(.enable("false"), .select(2), .width(8)) multiplexer_1 (
    .in0(proj1_ir2_ver2_1_ir_l), .in1(ram_1_dout), .in2(proj1_regfile_2b_1_outc),
    .in3(proj2_alu_implementation_1_outalu), .out(multiplexer_1_out), .sel(final_controlunit_1_muxasel));
  proj1_IR2_ver2 proj1_ir2_ver2_1 (
    .IR_L(proj1_ir2_ver2_1_ir_l), .IR_H(proj1_ir2_ver2_1_ir_h), .FunSel(final_controlunit_1_ir_funsel),
    .I(ram_1_dout), .H(final_controlunit_1_ir_selh), .Enable(final_controlunit_1_ir_enable));
  proj1_RegFile_2a proj1_regfile_2a_1 (
    .OutA(proj1_regfile_2a_1_outa), .OutB(proj1_regfile_2a_1_outb), .I(multiplexer_1_out),
    .RegSel(final_controlunit_1_gpr_regsel), .FunSel(final_controlunit_1_gpr_funsel),
    .OutASel(final_controlunit_1_outasel), .OutBSel(final_controlunit_1_outbsel));
  Multiplexer #(.enable("false"), .select(2), .width(8)) multiplexer_2 (
    .in1(proj1_ir2_ver2_1_ir_l), .in2(ram_1_dout), .in3(proj2_alu_implementation_1_outalu),
    .out(multiplexer_2_out), .sel(final_controlunit_1_muxbsel));  // open: in0
  Multiplexer #(.enable("false"), .width(8)) multiplexer_3 (
    .in0(proj1_regfile_2b_1_outc), .in1(proj1_regfile_2a_1_outa), .out(multiplexer_3_out),
    .sel(final_controlunit_1_muxcsel));
  proj2_ALU_implementation proj2_alu_implementation_1 (
    .OutAlu(proj2_alu_implementation_1_outalu), .Flags_ZCNO(proj2_alu_implementation_1_flags_zcno),
    .FunSel(final_controlunit_1_alu_funsel), .A(multiplexer_3_out), .B(proj1_regfile_2a_1_outb),
    .Cin(proj2_flagregister_1_c));
  proj2_flagRegister proj2_flagregister_1 (
    .C(proj2_flagregister_1_c), .Z(proj2_flagregister_1_z), .in_1(proj2_alu_implementation_1_flags_zcno));  // open: O, N
  proj1_RegFile_2b proj1_regfile_2b_1 (
    .OutC(proj1_regfile_2b_1_outc), .OutD(proj1_regfile_2b_1_outd), .I(multiplexer_2_out),
    .RegSel(final_controlunit_1_ar_regsel), .FunSel(final_controlunit_1_ar_funsel),
    .OutCSel(final_controlunit_1_outcsel), .OutDSel(final_controlunit_1_outdsel));
  Clock clock_1 (.out(clock_1_out));
  RAM #(.asyncread("true"), .\type ("nonvolatile")) ram_1 (
    .addr(proj1_regfile_2b_1_outd), .we(final_controlunit_1_ram_writeenable), .oe(1'b1), .clk(clock_1_out),
    .din(proj2_alu_implementation_1_outalu), .dout(ram_1_dout));
  final_controlUnit final_controlunit_1 (
    .IR_FunSel(final_controlunit_1_ir_funsel), .IR_Enable(final_controlunit_1_ir_enable),
    .MuxCSel(final_controlunit_1_muxcsel), .MuxASel(final_controlunit_1_muxasel),
    .OutASel(final_controlunit_1_outasel), .OutBSel(final_controlunit_1_outbsel),
    .GPR_RegSel(final_controlunit_1_gpr_regsel), .GPR_FunSel(final_controlunit_1_gpr_funsel),
    .ALU_FunSel(final_controlunit_1_alu_funsel), .RAM_WriteEnable(final_controlunit_1_ram_writeenable),
    .AR_RegSel(final_controlunit_1_ar_regsel), .OutCSel(final_controlunit_1_outcsel),
    .MuxBSel(final_controlunit_1_muxbsel), .AR_FunSel(final_controlunit_1_ar_funsel),
    .OutDSel(final_controlunit_1_outdsel), .IR_selH(final_controlunit_1_ir_selh), .Z(proj2_flagregister_1_z),
    .IR_H(proj1_ir2_ver2_1_ir_h), .IR_L(proj1_ir2_ver2_1_ir_l));
endmodule

module proj3_sequenceCounter (
  input  RESET,
  input  CLOCK,
  output [2:0] cOUT
);

  Counter #(.max('h7), .width(3)) counter_1 (
    .clr(RESET), .load(1'b0), .up(1'b1), .count(1'b1), .clk(CLOCK), .Q(cOUT));  // open: D, carry
  Hex_Digit_Display hex_digit_display_1 (.value({1'b0, cOUT}));  // open: dp
endmodule

module final_controlUnit (
  input  [7:0] IR_H,
  input  [7:0] IR_L,
  input  Z,
  output [2:0] AR_RegSel,
  output [1:0] OutCSel,
  output [1:0] MuxBSel,
  output [1:0] AR_FunSel,
  output [1:0] OutDSel,
  output IR_selH,
  output [1:0] IR_FunSel,
  output IR_Enable,
  output MuxCSel,
  output [1:0] MuxASel,
  output [1:0] OutASel,
  output [1:0] OutBSel,
  output [3:0] GPR_RegSel,
  output [1:0] GPR_FunSel,
  output [3:0] ALU_FunSel,
  output RAM_WriteEnable
);

  wire and_2_out, and_8_out, and_9_out, and_10_out, and_11_out, and_16_out, clock_1_out,
       controlled_buffer_1_out, decoder_1_out4, decoder_1_out5, decoder_2_out4, decoder_2_out5,
       decoder_5_out4, decoder_5_out5, dstreg_AR, fakeSrc, is_ARtoGPR, is_GPRtoAR_or_ARtoAR, isBNE,
       isDstReg_AR, isDstReg_GPR, isNotFetching, isSrcReg1_AR, isSrcReg1_GPR, srcreg1_AR, srcreg2_AR,
       srcreg2_PC, srcreg2_R0, srcreg2_R1, srcreg2_R2, srcreg2_R3, srcreg2_SP;
  wire [0:0] srcreg1_AR_packed;
  wire [1:0] final_controlunit_funsel_enablecontroller_1_forward,
       final_controlunit_outsel_forwarder_4_forward, int_AFunSel_Content, int_FunSel_Content, int_MuxCSel,
       regsel_map, srcreg1_GPR_map, srcreg2_GPR_map;
  wire [1:1] srcreg1_AR_map;
  wire [2:0] dstreg_AR_packed, final_controlunit_aregsel_forwarder_1_forward, int_AFunSel_Enable,
       int_aluFunSel_Enable, int_ARegSel, int_FunSel_Enable, int_OutASel, int_OutBSel, int_OutCSel,
       int_OutDSel, int_RegSel, multiplexer_1_out, proj3_sequencecounter_1_cout, subtractor_1_out;
  wire [2:1] and_4_out;
  wire [3:0] dstreg_GPR_packed, int_aluFunSel_Content, regsel_packed, srcreg1_GPR_packed;
  wire [4:0] multiplexer_2_out;
  wire [7:0] decoder_3_out0;
  wire [18:0] controlled_buffer_2_out;
  wire [23:0] rom_1_p2, rom_1_p3;

  Hex_Digit_Display hex_digit_display_1 (.value(IR_H[3:0]));  // open: dp
  Hex_Digit_Display hex_digit_display_2 (.value(IR_H[7:4]));  // open: dp
  or or_1 (isDstReg_AR, dstreg_AR_packed[2], dstreg_AR, dstreg_AR_packed[0]);
  Hex_Digit_Display hex_digit_display_3 (.value(IR_L[7:4]), .dp(IR_L[4]));
  Hex_Digit_Display hex_digit_display_4 (.value(IR_L[3:0]));  // open: dp
  Decoder #(.enable("false"), .select(3)) decoder_1 (
    .out0(dstreg_GPR_packed[0]), .out1(dstreg_GPR_packed[1]), .out2(dstreg_GPR_packed[2]),
    .out3(dstreg_GPR_packed[3]), .out4(decoder_1_out4), .out5(decoder_1_out5), .out6(dstreg_AR),
    .out7(dstreg_AR_packed[2]), .sel(IR_H[2:0]));
  Clock clock_1 (.out(clock_1_out));
  or or_2 (dstreg_AR_packed[0], decoder_1_out4, decoder_1_out5);
  Decoder #(.enable("false"), .select(3)) decoder_2 (
    .out0(srcreg1_GPR_packed[0]), .out1(srcreg1_GPR_packed[1]), .out2(srcreg1_GPR_packed[2]),
    .out3(srcreg1_GPR_packed[3]), .out4(decoder_2_out4), .out5(decoder_2_out5), .out6(srcreg1_AR),
    .out7(srcreg1_AR_map[1]), .sel(multiplexer_1_out));
  Multiplexer #(.enable("false"), .width(3)) multiplexer_1 (
    .in0(IR_L[7:5]), .in1(IR_H[2:0]), .out(multiplexer_1_out), .sel(fakeSrc));
  proj3_sequenceCounter proj3_sequencecounter_1 (
    .cOUT(proj3_sequencecounter_1_cout), .RESET(controlled_buffer_1_out), .CLOCK(clock_1_out));
  Subtractor #(.width(3)) subtractor_1 (
    .a(proj3_sequencecounter_1_cout), .b(3'b010), .out(subtractor_1_out));  // open: bin, bout
  and and_1 (and_4_out[2], ~subtractor_1_out[2], subtractor_1_out[1]);  // AND_Gate
  Multiplexer #(.enable("false"), .width(5)) multiplexer_2 (
    .in0(IR_H[7:3]), .in1({5{1'b1}}), .out(multiplexer_2_out), .sel(and_2_out));
  and and_2 (and_2_out, ~IR_H[7], ~IR_H[6], ~IR_H[5], ~IR_H[4], ~IR_H[3], IR_H[0]);  // AND_Gate
  and and_3 (isBNE, ~IR_H[3], ~IR_H[4], ~IR_H[5], ~IR_H[6], IR_H[7]);  // AND_Gate
  or or_3 (isDstReg_GPR, dstreg_GPR_packed[0], dstreg_GPR_packed[1], dstreg_GPR_packed[2], dstreg_GPR_packed[3]);
  and and_4 (and_4_out[1], ~subtractor_1_out[2], subtractor_1_out[0]);  // AND_Gate
  or or_4 (srcreg1_AR_packed[0], decoder_2_out4, decoder_2_out5);
  or or_5 (isSrcReg1_GPR, srcreg1_GPR_packed[0], srcreg1_GPR_packed[1], srcreg1_GPR_packed[2], srcreg1_GPR_packed[3]);
  Decoder #(.enable("false"), .select(3)) decoder_3 (
    .out0(decoder_3_out0[0]), .out1(decoder_3_out0[1]), .out2(decoder_3_out0[2]), .out3(decoder_3_out0[3]),
    .out4(decoder_3_out0[4]), .out5(decoder_3_out0[5]), .out6(decoder_3_out0[6]), .out7(decoder_3_out0[7]),
    .sel(proj3_sequencecounter_1_cout));
  // ROM #(.dataWidth(24), .line("dual")) rom_1: pin names not known; wires that end beside it: {multiplexer_2_out, and_4_out, 1'b0}, rom_1_p2, rom_1_p3
  nor nor_1 (isNotFetching, decoder_3_out0[0], decoder_3_out0[1]);
  Decoder #(.enable("false"), .select(2)) decoder_4 (
    .out0(regsel_packed[0]), .out1(regsel_packed[1]), .out2(regsel_packed[2]), .out3(regsel_packed[3]),
    .sel(IR_H[2:1]));
  Decoder #(.enable("false"), .select(3)) decoder_5 (
    .out0(srcreg2_R0), .out1(srcreg2_R1), .out2(srcreg2_R2), .out3(srcreg2_R3), .out4(decoder_5_out4),
    .out5(decoder_5_out5), .out6(srcreg2_AR), .out7(srcreg2_SP), .sel(IR_L[4:2]));
  or or_6 (isSrcReg1_AR, srcreg1_AR_packed[0], srcreg1_AR, srcreg1_AR_map[1]);
  proj3_controlUnit_fetch proj3_controlunit_fetch_1 (
    .ARegSel(AR_RegSel), .AFunSel(AR_FunSel), .OutDSel(OutDSel), .IR_selH(IR_selH), .IR_FunSel(IR_FunSel),
    .IR_Enable(IR_Enable), .Counter(decoder_3_out0));
  or or_7 (srcreg2_PC, decoder_5_out4, decoder_5_out5);
  assign controlled_buffer_1_out = isNotFetching ? controlled_buffer_2_out[0] : 1'bz;  // Controlled_Buffer controlled_buffer_1
  assign {int_ARegSel, int_AFunSel_Enable, int_AFunSel_Content, int_RegSel, int_FunSel_Enable, int_FunSel_Content, int_OutASel, int_OutBSel, int_OutCSel, int_OutDSel, MuxASel[1], controlled_buffer_2_out[18], MuxBSel, int_MuxCSel, IR_selH, IR_FunSel, IR_Enable, int_aluFunSel_Enable, int_aluFunSel_Content, RAM_WriteEnable, fakeSrc, controlled_buffer_2_out[0]} = isNotFetching ? {rom_1_p2, rom_1_p3} : 48'bz;  // Controlled_Buffer controlled_buffer_2
  and and_5 (is_ARtoGPR, isSrcReg1_AR, isDstReg_GPR);
  and and_6 (regsel_map[1], ~regsel_packed[0], ~regsel_packed[1]);  // AND_Gate
  and and_7 (regsel_map[0], ~regsel_packed[2], ~regsel_packed[0]);  // AND_Gate
  and and_8 (and_8_out, isSrcReg1_GPR, isDstReg_AR);
  and and_9 (and_9_out, isSrcReg1_AR, isDstReg_AR);
  and and_10 (and_10_out, ~MuxASel[1], controlled_buffer_2_out[18]);  // AND_Gate
  or or_8 (MuxASel[0], and_10_out, and_11_out);
  and and_11 (and_11_out, controlled_buffer_2_out[18], ~is_ARtoGPR);  // AND_Gate
  and and_12 (srcreg1_GPR_map[1], ~srcreg1_GPR_packed[0], ~srcreg1_GPR_packed[1]);  // AND_Gate
  and and_13 (srcreg1_GPR_map[0], ~srcreg1_GPR_packed[2], ~srcreg1_GPR_packed[0]);  // AND_Gate
  and and_14 (srcreg2_GPR_map[1], ~srcreg2_R0, ~srcreg2_R1);  // AND_Gate
  and and_15 (srcreg2_GPR_map[0], ~srcreg2_R2, ~srcreg2_R0);  // AND_Gate
  and and_16 (and_16_out, isSrcReg1_GPR, isDstReg_GPR);
  final_controlUnit_OUTSEL_forwarder final_controlunit_outsel_forwarder_1 (
    .forward(OutASel), .regsel_map(regsel_map), .srcreg1_GPR_map(srcreg1_GPR_map),
    .srcreg2_GPR_map(srcreg2_GPR_map), .outsel(int_OutASel), .srcreg1_AR_map({srcreg1_AR_map[1], srcreg1_AR}));
  final_controlUnit_OUTSEL_forwarder final_controlunit_outsel_forwarder_2 (
    .forward(OutCSel), .regsel_map(regsel_map), .srcreg1_GPR_map(srcreg1_GPR_map),
    .srcreg2_GPR_map(srcreg2_GPR_map), .outsel(int_OutCSel), .srcreg1_AR_map({srcreg1_AR_map[1], srcreg1_AR}));
  or or_9 (is_GPRtoAR_or_ARtoAR, and_8_out, and_16_out, and_9_out);
  final_controlUnit_ARegSel_forwarder final_controlunit_aregsel_forwarder_1 (
    .forward(final_controlunit_aregsel_forwarder_1_forward),
    .srcreg1_AR_packed({srcreg1_AR_map[1], srcreg1_AR, srcreg1_AR_packed[0]}),
    .dstreg_AR_packed({dstreg_AR_packed[2], dstreg_AR, dstreg_AR_packed[0]}), .regsel(int_ARegSel));
  final_controlUnit_RegSel_forwarder final_controlunit_regsel_forwarder_1 (
    .forward(GPR_RegSel), .srcreg1_GPR_packed(srcreg1_GPR_packed), .regsel_packed(regsel_packed),
    .dstreg_GPR_packed(dstreg_GPR_packed), .regsel(int_RegSel));
  final_controlUnit_MuxCSel_Forwarder final_controlunit_muxcsel_forwarder_1 (
    .forward(MuxCSel), .isSrcReg1_AR(isSrcReg1_AR), .MuxCSel(int_MuxCSel));
  final_controlUnit_ALUFunsel_enableController final_controlunit_alufunsel_enablecontroller_1 (
    .forward(ALU_FunSel), .is_ZFlagSet(Z), .isDstReg_GPR(isDstReg_GPR), .isDstReg_AR(isDstReg_AR),
    .is_GPRtoAR_or_ARtoAR(is_GPRtoAR_or_ARtoAR), .isSrcReg1_AR(isSrcReg1_AR), .isSrcReg1_GPR(isSrcReg1_GPR),
    .content(int_aluFunSel_Content), .enable(int_aluFunSel_Enable), .isBNE(isBNE));
  final_controlUnit_FunSel_enableController final_controlunit_funsel_enablecontroller_1 (
    .forward(final_controlunit_funsel_enablecontroller_1_forward), .is_ZFlagSet(Z),
    .isDstReg_GPR(isDstReg_GPR), .isDstReg_AR(isDstReg_AR), .is_GPRtoAR_or_ARtoAR(is_GPRtoAR_or_ARtoAR),
    .isSrcReg1_AR(isSrcReg1_AR), .isSrcReg1_GPR(isSrcReg1_GPR), .content(int_AFunSel_Content),
    .enable(int_AFunSel_Enable), .isBNE(isBNE));
  final_controlUnit_FunSel_enableController final_controlunit_funsel_enablecontroller_2 (
    .forward(GPR_FunSel), .is_ZFlagSet(Z), .isDstReg_GPR(isDstReg_GPR), .isDstReg_AR(isDstReg_AR),
    .is_GPRtoAR_or_ARtoAR(is_GPRtoAR_or_ARtoAR), .isSrcReg1_AR(isSrcReg1_AR), .isSrcReg1_GPR(isSrcReg1_GPR),
    .content(int_FunSel_Content), .enable(int_FunSel_Enable), .isBNE(isBNE));
  final_controlUnit_OUTSEL_forwarder final_controlunit_outsel_forwarder_3 (
    .forward(OutBSel), .regsel_map(regsel_map), .srcreg1_GPR_map(srcreg1_GPR_map),
    .srcreg2_GPR_map(srcreg2_GPR_map), .outsel(int_OutBSel), .srcreg1_AR_map({srcreg1_AR_map[1], srcreg1_AR}));
  final_controlUnit_OUTSEL_forwarder final_controlunit_outsel_forwarder_4 (
    .forward(final_controlunit_outsel_forwarder_4_forward), .regsel_map(regsel_map),
    .srcreg1_GPR_map(srcreg1_GPR_map), .srcreg2_GPR_map(srcreg2_GPR_map), .outsel(int_OutDSel),
    .srcreg1_AR_map({srcreg1_AR_map[1], srcreg1_AR}));
  assign AR_RegSel = isNotFetching ? final_controlunit_aregsel_forwarder_1_forward : 3'bz;  // Controlled_Buffer controlled_buffer_3
  assign AR_FunSel = isNotFetching ? final_controlunit_funsel_enablecontroller_1_forward : 2'bz;  // Controlled_Buffer controlled_buffer_4
  assign OutDSel = isNotFetching ? final_controlunit_outsel_forwarder_4_forward : 2'bz;  // Controlled_Buffer controlled_buffer_5
  // Pins of 1 and 4 bits meet at IR_L[7:4]

  // Other names for the same wires on the sheet: dstreg_signal[2:0] = IR_H[2:0]; AFunSel[1:0] = AR_FunSel;
  //   ARegSel[2:0] = AR_RegSel; dstreg_PC = dstreg_AR_packed[0]; dstreg_AR_packed[1] = dstreg_AR;
  //   dstreg_SP = dstreg_AR_packed[2]; dstreg_R0 = dstreg_GPR_packed[0]; dstreg_R1 = dstreg_GPR_packed[1];
  //   dstreg_R2 = dstreg_GPR_packed[2]; dstreg_R3 = dstreg_GPR_packed[3]; FunSel[1:0] = GPR_FunSel;
  //   FunSelAlu[3:0] = ALU_FunSel; srcreg1_signal[2:0] = IR_L[7:5]; RegSel[3:0] = GPR_RegSel;
  //   regsel_R0 = regsel_packed[0]; regsel_R1 = regsel_packed[1]; regsel_R2 = regsel_packed[2];
  //   regsel_R3 = regsel_packed[3]; srcreg1_AR_map[0] = srcreg1_AR;
  //   srcreg1_AR_packed[2:1] = {srcreg1_AR_map[1], srcreg1_AR}; srcreg1_SP = srcreg1_AR_map[1];
  //   srcreg1_PC = srcreg1_AR_packed[0]; srcreg1_R0 = srcreg1_GPR_packed[0]; srcreg1_R1 = srcreg1_GPR_packed[1];
  //   srcreg1_R2 = srcreg1_GPR_packed[2]; srcreg1_R3 = srcreg1_GPR_packed[3]

  // Notes on the sheet:
  //   --special case for load--
  //   --special case for BNE--
  //   contents of rom_1 (hex, n*v repeats v):
  //   a500 0 0 1 4*0 60 104084 0 1 4*0 cde9a3 f8280 0 1 4*0 c 20008c 870000 0 0 1 0 0 860000 0 a500 240000
  //   0 1 0 0 cde9bf f80a0 0 1 4*0 cde9bf f80b0 0 1 4*0 5b7f00 0 cde9a3 f8280 cde9a3 f8282 0 1 5a7e00 0
  //   cde9a3 f8280 cde9a3 f8282 0 1 cde9bf f80b8 0 1 4*0 cde9bf f80c0 0 1 4*0 cde9bf f8090 0 1 4*0 cde9bf
  //   f80d0 0 1 4*0 cde9bf f80d8 0 1 4*0 250000 10000 0 1 4*0 310000 10000 0 1 4*0 310000 10000 0 1 4*0
  //   870000 200084 250000 10000 0 1 0 0 860000 0 250000 220000 0 1 98*0 a500 140000 0 1
endmodule

module proj3_controlUnit_fetch (
  input  [7:0] Counter,
  output [2:0] ARegSel,
  output [1:0] AFunSel,
  output [1:0] OutDSel,
  output IR_selH,
  output [1:0] IR_FunSel,
  output IR_Enable
);

  assign OutDSel = Counter[0] ? 2'b00 : 2'bz;  // Controlled_Buffer controlled_buffer_1
  assign ARegSel = Counter[1] ? 3'b001 : 3'bz;  // Controlled_Buffer controlled_buffer_2
  assign IR_Enable = Counter[0] ? 1'b1 : 1'bz;  // Controlled_Buffer controlled_buffer_3
  assign AFunSel = Counter[1] ? 2'b10 : 2'bz;  // Controlled_Buffer controlled_buffer_4
  assign IR_FunSel = Counter[0] ? 2'b11 : 2'bz;  // Controlled_Buffer controlled_buffer_5
  assign IR_selH = Counter[1] ? 1'b0 : 1'bz;  // Controlled_Buffer controlled_buffer_6
  assign OutDSel = Counter[1] ? 2'b00 : 2'bz;  // Controlled_Buffer controlled_buffer_7
  assign ARegSel = Counter[0] ? 3'b001 : 3'bz;  // Controlled_Buffer controlled_buffer_8
  assign AFunSel = Counter[0] ? 2'b10 : 2'bz;  // Controlled_Buffer controlled_buffer_9
  assign IR_Enable = Counter[1] ? 1'b1 : 1'bz;  // Controlled_Buffer controlled_buffer_10
  assign IR_selH = Counter[0] ? 1'b1 : 1'bz;  // Controlled_Buffer controlled_buffer_11
  assign IR_FunSel = Counter[1] ? 2'b11 : 2'bz;  // Controlled_Buffer controlled_buffer_12
endmodule

module final_controlUnit_OUTSEL_forwarder (
  input  [1:0] regsel_map,
  input  [1:0] srcreg1_GPR_map,
  input  [1:0] srcreg1_AR_map,
  input  [1:0] srcreg2_GPR_map,
  input  [2:0] outsel,
  output [1:0] forward
);

  Multiplexer #(.enable("false"), .select(3), .width(2)) multiplexer_1 (
    .in0(2'b00), .in1(2'b01), .in2(2'b10), .in3(regsel_map), .in4(2'b00), .in5(srcreg1_GPR_map),
    .in6(srcreg1_AR_map), .in7(srcreg2_GPR_map), .out(forward), .sel(outsel));
endmodule

module final_controlUnit_FunSel_enableController (
  input  isBNE,
  input  [1:0] content,
  input  isDstReg_GPR,
  input  isDstReg_AR,
  input  is_ZFlagSet,
  input  is_GPRtoAR_or_ARtoAR,
  input  isSrcReg1_AR,
  input  isSrcReg1_GPR,
  input  [2:0] enable,
  output [1:0] forward
);

  wire and_1_out, and_2_out, or_1_out;
  wire [1:0] controlled_buffer_1_out, controlled_buffer_2_out, controlled_buffer_3_out,
       controlled_buffer_4_out, controlled_buffer_5_out, controlled_buffer_6_out, undriven;

  and and_1 (and_1_out, isBNE, ~is_ZFlagSet);  // AND_Gate
  and and_2 (and_2_out, ~isBNE, is_ZFlagSet);  // AND_Gate
  or or_1 (or_1_out, and_1_out, and_2_out);
  assign controlled_buffer_1_out = isDstReg_GPR ? content : 2'bz;  // Controlled_Buffer controlled_buffer_1
  assign controlled_buffer_2_out = isDstReg_AR ? content : 2'bz;  // Controlled_Buffer controlled_buffer_2
  assign controlled_buffer_3_out = or_1_out ? content : 2'bz;  // Controlled_Buffer controlled_buffer_3
  assign controlled_buffer_4_out = isSrcReg1_AR ? content : 2'bz;  // Controlled_Buffer controlled_buffer_4
  // NoConnect on undriven
  assign controlled_buffer_5_out = is_GPRtoAR_or_ARtoAR ? content : 2'bz;  // Controlled_Buffer controlled_buffer_5
  assign controlled_buffer_6_out = isSrcReg1_GPR ? content : 2'bz;  // Controlled_Buffer controlled_buffer_6
  Multiplexer #(.disabled("Z"), .enable("false"), .select(3), .width(2)) multiplexer_1 (
    .in0(undriven), .in1(content), .in2(controlled_buffer_1_out), .in3(controlled_buffer_2_out),
    .in4(controlled_buffer_3_out), .in5(controlled_buffer_5_out), .in6(controlled_buffer_4_out),
    .in7(controlled_buffer_6_out), .out(forward), .sel(enable));
endmodule

module final_controlUnit_ALUFunsel_enableController (
  input  isBNE,
  input  [3:0] content,
  input  isDstReg_GPR,
  input  isDstReg_AR,
  input  is_ZFlagSet,
  input  is_GPRtoAR_or_ARtoAR,
  input  isSrcReg1_AR,
  input  isSrcReg1_GPR,
  input  [2:0] enable,
  output [3:0] forward
);

  wire and_1_out, and_2_out, or_1_out;
  wire [3:0] controlled_buffer_1_out, controlled_buffer_2_out, controlled_buffer_3_out,
       controlled_buffer_4_out, controlled_buffer_5_out, controlled_buffer_6_out, undriven;

  and and_1 (and_1_out, isBNE, ~is_ZFlagSet);  // AND_Gate
  and and_2 (and_2_out, ~isBNE, is_ZFlagSet);  // AND_Gate
  or or_1 (or_1_out, and_1_out, and_2_out);
  assign controlled_buffer_1_out = isDstReg_GPR ? content : 4'bz;  // Controlled_Buffer controlled_buffer_1
  assign controlled_buffer_2_out = isDstReg_AR ? content : 4'bz;  // Controlled_Buffer controlled_buffer_2
  assign controlled_buffer_3_out = or_1_out ? content : 4'bz;  // Controlled_Buffer controlled_buffer_3
  assign controlled_buffer_4_out = isSrcReg1_AR ? content : 4'bz;  // Controlled_Buffer controlled_buffer_4
  // NoConnect on undriven
  assign controlled_buffer_5_out = is_GPRtoAR_or_ARtoAR ? content : 4'bz;  // Controlled_Buffer controlled_buffer_5
  assign controlled_buffer_6_out = isSrcReg1_GPR ? content : 4'bz;  // Controlled_Buffer controlled_buffer_6
  Multiplexer #(.enable("false"), .select(3), .width(4)) multiplexer_1 (
    .in0(undriven), .in1(content), .in2(controlled_buffer_1_out), .in3(controlled_buffer_2_out),
    .in4(controlled_buffer_3_out), .in5(controlled_buffer_5_out), .in6(controlled_buffer_4_out),
    .in7(controlled_buffer_6_out), .out(forward), .sel(enable));
endmodule

module final_controlUnit_MuxCSel_Forwarder (
  input  isSrcReg1_AR,
  input  [1:0] MuxCSel,
  output forward
);

  wire not_1_out;

  not not_1 (not_1_out, isSrcReg1_AR);
  Multiplexer #(.enable("false"), .select(2)) multiplexer_1 (
    .in0(1'b0), .in1(1'b1), .in2(not_1_out), .in3(1'b0), .out(forward), .sel(MuxCSel));
endmodule

module final_controlUnit_ARegSel_forwarder (
  input  [2:0] srcreg1_AR_packed,
  input  [2:0] dstreg_AR_packed,
  input  [2:0] regsel,
  output [2:0] forward
);

  wire [2:0] undriven, undriven_2, undriven_3;

  // NoConnect on undriven
  // NoConnect on undriven_2
  // NoConnect on undriven_3
  Multiplexer #(.enable("false"), .select(3), .width(3)) multiplexer_1 (
    .in0(3'b000), .in1(3'b001), .in2(srcreg1_AR_packed), .in3(undriven), .in4(3'b100), .in5(undriven_2),
    .in6(dstreg_AR_packed), .in7(undriven_3), .out(forward), .sel(regsel));
endmodule

module final_controlUnit_RegSel_forwarder (
  input  [3:0] srcreg1_GPR_packed,
  input  [3:0] regsel_packed,
  input  [3:0] dstreg_GPR_packed,
  input  [2:0] regsel,
  output [3:0] forward
);

  wire [3:0] undriven, undriven_2;

  // NoConnect on undriven
  // NoConnect on undriven_2
  Multiplexer #(.enable("false"), .select(3), .width(4)) multiplexer_1 (
    .in0(4'b0000), .in1(4'b0001), .in2(undriven), .in3(srcreg1_GPR_packed), .in4(4'b0100),
    .in5(regsel_packed), .in6(undriven_2), .in7(dstreg_GPR_packed), .out(forward), .sel(regsel));
endmodule
